// Logisim project CPU.circ as structural Verilog: 1 circuit, main circuit main
module main (
);

  wire clock_1_out, decoder_1_out0, decoder_1_out1;
  wire [7:0] multiplexer_1_out, PC_q, ram_1_data, undriven;

  Clock clock_1 (.out(clock_1_out));
  Counter PC (.Q(PC_q), .clk(clock_1_out));  // open: load, D, count, carry, clr
  Multiplexer #(.width(8), .enable("false")) multiplexer_1 (
    .in0(PC_q), .in1(undriven), .out(multiplexer_1_out));  // open: sel
  RAM ram_1 (.addr(multiplexer_1_out), .data(ram_1_data));  // open: sel, clk, ld, clr
  Decoder decoder_1 (.out0(decoder_1_out0), .out1(decoder_1_out1), .en(1'b1));  // open: sel
  Register R_B (.D(ram_1_data), .clk(decoder_1_out1));  // open: en, Q, clr
  Register R_A (.D(ram_1_data), .clk(decoder_1_out0));  // open: en, Q, clr
  Register register_1 (.en(ram_1_data[0]), .clk(clock_1_out));  // open: D, Q, clr
  // Pins of 1 and 8 bits meet at ram_1_data
  // Pins of 6 and 8 bits meet at undriven

  // Notes on the sheet:
  //   PC
  //   IR
endmodule
